# Fritzing sketch schematic (saved by Fritzing 0.9.3b)
breadboards: 1

parts:
  M1 = DC Motor
  M2 = DC Motor
  Part1 = Arduino Nano (Rev3.0) (ICSP)
  U1 = L298 [package=multiwatt15]
  LED1 = LEDs [package=led10mm]
  LED2 = LEDs [package=led10mm]
  Q1 = LTR-301 [package=ltr-301]
  Q2 = LTR-301 [package=ltr-301]
  R1 = Resistor [tolerance=±5% resistance=220 package="2010 [SMD]"]
  R2 = Resistor [tolerance=±5% resistance=220 package="2010 [SMD]"]
  R3 = Resistor [tolerance=±5% resistance=2.2k package="0603 [SMD]"]
  R4 = Resistor [tolerance=±5% resistance=2.2k package="0603 [SMD]"]
  U2 = LIPO-1000mAh [package=lipo-1000]

nets:
  N1: M1.pin_1, U1.OUT1
  N2: M1.pin_2, U1.OUT2
  N3: M2.pin_1, U1.OUT3
  N4: M2.pin_2, U1.OUT4
  N5: Part1.D2, U1.IN4
  N6: Part1.D3, U1.IN3
  N7: Part1.D7, U1.IN2
  N8: Part1.D8, U1.IN1
  N9: Part1.VIN, U1.VS, U2.+
  GND: Part1.GND, U1.GND, LED2.C, Q1.E, Q2.E, U2.-
  N10: Part1.5V, U1.VLS, R2.Pin_1
  N11: Part1.A1, Q2.C, R3.Pin_0
  N12: Part1.A0, Q1.C, R4.Pin_0
  N13: LED1.C, R1.Pin_1
  N14: LED1.A, R2.Pin_0
  N15: LED2.A, R1.Pin_0
  N16: R3.Pin_1, R4.Pin_1
